// Logisim project RV32I_32bit_ALU.circ as structural Verilog: 1 circuit, main circuit ALU
module ALU (
  input  [31:0] A,
  input  [31:0] B,
  input  [4:0] Amount_To_Shift,
  input  [11:0] twelve_bit_input,
  input  [19:0] Immediate,
  input  [31:0] PC,
  input  [31:0] Instruction,
  output [31:0] Result
);

  wire and_2_out, and_3_out, and_4_out, and_5_out, and_6_out, and_7_out, comparator_1_lt, comparator_2_lt,
       comparator_3_eq, comparator_4_eq, comparator_5_eq, comparator_6_eq, comparator_7_eq, comparator_8_eq,
       comparator_9_eq, comparator_10_eq, comparator_11_eq, comparator_12_eq, comparator_13_eq,
       comparator_14_eq, comparator_16_eq, comparator_17_eq, comparator_18_eq, comparator_19_eq,
       comparator_20_eq, comparator_21_eq, I_TYPE, or_2_out, or_3_out, or_4_out, or_5_out, or_6_out, or_7_out;
  wire [3:0] priority_encoder_1_out;
  wire [4:0] SHIFTSEL5;
  wire [31:0] adder_1_out, adder_2_out, and_1_out, bit_extender_1_out, bit_extender_2_out,
       bit_extender_3_out, multiplexer_1_out, or_1_out, shifter_1_out, shifter_2_out, shifter_3_out,
       subtractor_1_out, xor_1_out;

  Multiplexer #(.width(32)) multiplexer_1 (.in0(B), .in1(bit_extender_3_out), .out(multiplexer_1_out), .sel(I_TYPE));
  Multiplexer #(.width(5)) multiplexer_2 (
    .in0(Amount_To_Shift), .in1(Instruction[24:20]), .out(SHIFTSEL5), .sel(I_TYPE));
  Adder #(.width(32)) adder_1 (.a(A), .b(multiplexer_1_out), .out(adder_1_out));  // open: cin, cout
  Subtractor #(.width(32)) subtractor_1 (.a(A), .b(multiplexer_1_out), .out(subtractor_1_out));  // open: bin, bout
  Shifter #(.width(32)) shifter_1 (.in(A), .\dist (SHIFTSEL5), .out(shifter_1_out));
  assign bit_extender_1_out = {{31{comparator_1_lt}}, comparator_1_lt};  // Bit_Extender bit_extender_1
  Comparator #(.width(32)) comparator_1 (.a(A), .b(multiplexer_1_out), .lt(comparator_1_lt));  // open: gt, eq
  assign bit_extender_2_out = {{31{comparator_2_lt}}, comparator_2_lt};  // Bit_Extender bit_extender_2
  Comparator #(.mode("unsigned"), .width(32)) comparator_2 (
    .a(A), .b(multiplexer_1_out), .lt(comparator_2_lt));  // open: gt, eq
  assign xor_1_out = A ^ multiplexer_1_out;  // XOR_Gate xor_1, 32 bits wide
  Shifter #(.shift("lr"), .width(32)) shifter_2 (.in(A), .\dist (SHIFTSEL5), .out(shifter_2_out));
  Shifter #(.shift("ar"), .width(32)) shifter_3 (.in(A), .\dist (SHIFTSEL5), .out(shifter_3_out));
  assign or_1_out = A | multiplexer_1_out;  // OR_Gate or_1, 32 bits wide
  assign and_1_out = A & multiplexer_1_out;  // AND_Gate and_1, 32 bits wide
  Adder #(.width(32)) adder_2 (.a({Immediate, twelve_bit_input}), .b(PC), .out(adder_2_out));  // open: cin, cout
  Comparator #(.width(10)) comparator_3 (
    .a({Instruction[31:25], Instruction[14:12]}), .b({10{1'b0}}), .eq(comparator_3_eq));  // open: gt, lt
  Comparator #(.width(10)) comparator_4 (
    .a({Instruction[31:25], Instruction[14:12]}), .b(10'h100), .eq(comparator_4_eq));  // open: gt, lt
  Comparator #(.width(10)) comparator_5 (
    .a({Instruction[31:25], Instruction[14:12]}), .b(10'h1), .eq(comparator_5_eq));  // open: gt, lt
  Comparator #(.width(10)) comparator_6 (
    .a({Instruction[31:25], Instruction[14:12]}), .b(10'h2), .eq(comparator_6_eq));  // open: gt, lt
  Comparator #(.width(10)) comparator_7 (
    .a({Instruction[31:25], Instruction[14:12]}), .b(10'h3), .eq(comparator_7_eq));  // open: gt, lt
  Comparator #(.width(10)) comparator_8 (
    .a({Instruction[31:25], Instruction[14:12]}), .b(10'h4), .eq(comparator_8_eq));  // open: gt, lt
  Comparator #(.width(10)) comparator_9 (
    .a({Instruction[31:25], Instruction[14:12]}), .b(10'h5), .eq(comparator_9_eq));  // open: gt, lt
  Comparator #(.width(10)) comparator_10 (
    .a({Instruction[31:25], Instruction[14:12]}), .b(10'h105), .eq(comparator_10_eq));  // open: gt, lt
  Comparator #(.width(10)) comparator_11 (
    .a({Instruction[31:25], Instruction[14:12]}), .b(10'h6), .eq(comparator_11_eq));  // open: gt, lt
  Comparator #(.width(10)) comparator_12 (
    .a({Instruction[31:25], Instruction[14:12]}), .b(10'h7), .eq(comparator_12_eq));  // open: gt, lt
  Comparator #(.width(7)) comparator_13 (.a(Instruction[6:0]), .b(7'b0110111), .eq(comparator_13_eq));  // open: gt, lt
  Comparator #(.width(7)) comparator_14 (.a(Instruction[6:0]), .b(7'b0010111), .eq(comparator_14_eq));  // open: gt, lt
  assign bit_extender_3_out = {{20{Instruction[31]}}, Instruction[31:20]};  // Bit_Extender bit_extender_3
  Comparator #(.width(7)) comparator_15 (.a(Instruction[6:0]), .b(7'b0010011), .eq(I_TYPE));  // open: gt, lt
  Comparator #(.width(3)) comparator_16 (.a(Instruction[14:12]), .b(3'b000), .eq(comparator_16_eq));  // open: gt, lt
  Comparator #(.width(3)) comparator_17 (.a(Instruction[14:12]), .b(3'b010), .eq(comparator_17_eq));  // open: gt, lt
  Comparator #(.width(3)) comparator_18 (.a(Instruction[14:12]), .b(3'b011), .eq(comparator_18_eq));  // open: gt, lt
  Comparator #(.width(3)) comparator_19 (.a(Instruction[14:12]), .b(3'b100), .eq(comparator_19_eq));  // open: gt, lt
  Comparator #(.width(3)) comparator_20 (.a(Instruction[14:12]), .b(3'b110), .eq(comparator_20_eq));  // open: gt, lt
  Comparator #(.width(3)) comparator_21 (.a(Instruction[14:12]), .b(3'b111), .eq(comparator_21_eq));  // open: gt, lt
  and and_2 (and_2_out, I_TYPE, comparator_16_eq);
  and and_3 (and_3_out, I_TYPE, comparator_17_eq);
  and and_4 (and_4_out, I_TYPE, comparator_18_eq);
  and and_5 (and_5_out, I_TYPE, comparator_19_eq);
  and and_6 (and_6_out, I_TYPE, comparator_20_eq);
  and and_7 (and_7_out, I_TYPE, comparator_21_eq);
  or or_2 (or_2_out, comparator_3_eq, and_2_out);
  or or_3 (or_3_out, comparator_6_eq, and_3_out);
  or or_4 (or_4_out, comparator_7_eq, and_4_out);
  or or_5 (or_5_out, comparator_8_eq, and_5_out);
  or or_6 (or_6_out, comparator_11_eq, and_6_out);
  or or_7 (or_7_out, comparator_12_eq, and_7_out);
  Multiplexer #(.select(4), .width(32)) multiplexer_3 (
    .in0(adder_1_out), .in1(subtractor_1_out), .in2(shifter_1_out), .in3(bit_extender_1_out),
    .in4(bit_extender_2_out), .in5(xor_1_out), .in6(shifter_2_out), .in7(shifter_3_out), .in8(or_1_out),
    .in9(and_1_out), .in10({Immediate, twelve_bit_input}), .in11(adder_2_out), .out(Result),
    .sel(priority_encoder_1_out));  // open: in12, in13, in14, in15
  Priority_Encoder #(.select(4)) priority_encoder_1 (
    .in0(or_2_out), .in1(comparator_4_eq), .in2(comparator_5_eq), .in3(or_3_out), .in4(or_4_out),
    .in5(or_5_out), .in6(comparator_9_eq), .in7(comparator_10_eq), .in8(or_6_out), .in9(or_7_out),
    .in10(comparator_13_eq), .in11(comparator_14_eq), .out(priority_encoder_1_out));  // open: in12, in13, in14, in15, gs, en_out, en_in

  // Other names for the same wires on the sheet: I_IMM12[11:0] = Instruction[31:20]; SHAMT5[4:0] = Instruction[24:20];
  //   R_SHAMT5[4:0] = Amount_To_Shift

  // Notes on the sheet:
  //   Shift amount select: R-type / I-type
  //   0 = Amount_To_Shift, 1 = Instruction[24:20]
  //   Shift amount MUX (5-bit): R-type / I-type
  //   I-type selects Instruction[24:20] (shamt)
  //   ALUSrc MUX: B / Immediate
  //   RV32I ALU - R-type, I-type, LUI, AUIPC
  //   Instruction Decoder
  //   I Type Immediate
  //   Opcode
  //   Function 3
  //   Function 7
  //   Adder
  //   Subtractor
  //   SLL
  //   SLT
  //   SLTU
  //   SRL
  //   SRA
  //   Shift-immediate shamt = Instruction[24:20]
  //   SLL / SLLI
  //   XOR
  //   SRL / SRLI
  //   SRA / SRAI
  //   OR
  //   AND
  //   Upper Immediate [31:12]
  //   LUI
  //   AUIPC
  //   SLT: signed comparison
  //   SLTU: unsigned comparison
  //   ADD decode
  //   SUB decode
  //   SLL decode
  //   SLT decode
  //   SLTU decode
  //   XOR decode
  //   SRL decode
  //   SRA decode
  //   OR decode
  //   AND decode
  //   LUI opcode 0x37
  //   AUIPC opcode 0x17
  //   ADDI
  //   SLTI
  //   SLTIU
  //   XORI
  //   ORI
  //   ANDI
  //   12 -> 32 Sign Extend
  //   I-type opcode 0x13
  //   ADDI select
  //   SLTI select
  //   SLTIU select
  //   XORI select
  //   ORI select
  //   ANDI select
  //   32-bit Result MUX
  //   ALU Result Output
  //   Instruction Priority Encoder
endmodule
